// Logisim project Vending_Machine_2.circ as structural Verilog: 1 circuit, main circuit main
module main (
  input  x1,
  input  x2,
  output x1x2,
  output x1x2_2,
  output x1_x2,
  output x1_x2_2,
  output Y1,
  output Y2,
  output Z1,
  output Z2
);

  wire D1_p1, D1_p3, Delay_p2, Delay_p6, n7404_1_p2, n7404_1_p4, n7408_1_p3, n7408_1_p5, n7408_1_p6,
       n7408_1_p7, n7408_1_p9, n7408_3_p3, n7408_3_p6, n7408_3_p7, n7408_3_p8, n7408_3_p9, n7408_3_p10,
       n7408_3_p12, n7408_4_p6, n7432_1_p3, n7432_2_p6, n7432_3_p3, n7432_3_p6, n7432_3_p8;

  // _7404 7404_1: pin names not known; wires that end beside it: x1, n7404_1_p2, x2, n7404_1_p4
  // _7408 7408_1: pin names not known; wires that end beside it: x1_x2_2, Y1, n7408_1_p3, x1_x2, n7408_1_p5, n7408_1_p6, n7408_1_p7, Y2, n7408_1_p9
  // _7432 7432_1: pin names not known; wires that end beside it: n7408_1_p9, n7408_1_p6, n7432_1_p3, x1_x2_2, x1x2, n7408_1_p7
  // _7408 7408_2: pin names not known; wires that end beside it: x1, n7404_1_p4, x1x2_2, n7404_1_p2, x2, x1_x2, x1, x2, x1x2, n7404_1_p2, n7404_1_p4, x1_x2_2
  // _7408 7408_3: pin names not known; wires that end beside it: Y2, n7404_1_p2, n7408_3_p3, n7408_1_p5, x2, n7408_3_p6, n7408_3_p7, n7408_3_p8, n7408_3_p9, n7408_3_p10, Y1, n7408_3_p12
  // _7432 7432_2: pin names not known; wires that end beside it: x1_x2_2, n7408_3_p3, n7408_3_p8, n7408_3_p9, n7408_3_p12, n7432_2_p6, x1x2, n7408_3_p6, n7408_3_p10
  // _7474 D1: pin names not known; wires that end beside it: D1_p1, n7432_2_p6, D1_p3, Y1, n7408_3_p7
  // _7474 D2: pin names not known; wires that end beside it: D1_p1, n7432_1_p3, D1_p3, Y2, n7408_1_p5
  // _7474 Delay: pin names not known; wires that end beside it: D1_p1, Delay_p2, D1_p3, Z1, D1_p1, Delay_p6, D1_p3, Z2
  // _7432 7432_3: pin names not known; wires that end beside it: Y2, Y1, n7432_3_p3, n7408_1_p3, x1x2, n7432_3_p6, n7432_3_p6, n7432_3_p8, Delay_p2
  Clock Clock (.out(D1_p3));
  Button Clear (.out(D1_p1));
  // _7408 7408_4: pin names not known; wires that end beside it: n7432_3_p3, x1x2_2, Delay_p6, Y2, Y1, n7408_4_p6, n7408_4_p6, x2, n7432_3_p8
endmodule
